// Logisim project KrajcovicPPI01.circ as structural Verilog: 1 circuit, main circuit main
module main (
  input  D,
  input  C,
  input  B,
  input  A,
  output Y,
  output Z,
  output Y_DNF,
  output Z_DNF,
  output Y_KNF,
  output Z_KNF
);

  wire and_1_out, and_2_out, and_3_out, and_4_out, and_5_out, and_6_out, and_7_out, nand_1_out, nand_2_out,
       nand_3_out, not_1_out, not_2_out, not_3_out, not_4_out, not_5_out, or_1_out, or_2_out, or_3_out,
       or_4_out, or_5_out, or_6_out;

  not not_1 (not_1_out, D);
  not not_2 (not_2_out, C);
  not not_3 (not_3_out, B);
  not not_4 (not_4_out, D);
  not not_5 (not_5_out, A);
  and and_1 (and_1_out, not_5_out, not_2_out);
  and and_2 (and_2_out, not_5_out, D);
  and and_3 (and_3_out, not_3_out, not_2_out);
  and and_4 (and_4_out, not_3_out, D);
  and and_5 (and_5_out, A, B, C, not_1_out);
  and and_6 (and_6_out, B, D);
  and and_7 (and_7_out, C, not_1_out);
  or or_1 (or_1_out, not_3_out, not_5_out, D);
  or or_2 (or_2_out, B, not_2_out, D);
  or or_3 (or_3_out, not_5_out, not_3_out, C);
  or or_4 (or_4_out, not_5_out, not_3_out, not_1_out);
  or or_5 (or_5_out, B, not_1_out);
  or or_6 (or_6_out, C, D);
  nand nand_1 (nand_1_out, A, B);
  nand nand_2 (nand_2_out, C, not_4_out);
  nand nand_3 (nand_3_out, B, D);
  xnor xnor_1 (Y, nand_1_out, nand_2_out);
  xor xor_1 (Z, nand_2_out, nand_3_out);
  or or_7 (Y_DNF, and_1_out, and_2_out, and_3_out, and_4_out, and_5_out);
  or or_8 (Z_DNF, and_6_out, and_7_out);
  and and_8 (Y_KNF, or_1_out, or_2_out, or_3_out, or_4_out);
  and and_9 (Z_KNF, or_5_out, or_6_out);

  // Notes on the sheet:
  //   D
  //   C
  //   C'
  //   D'
  //   D'
  //   C
  //   D
  //   D'
  //   D
  //   C
  //   D
  //   C
  //   D'
  //   C
  //   D
  //   D'
  //   A
  //   B
  //   B'
  //   A'
  //   C'
  //   B'
  //   A
  //   B
  //   B'
  //   C'
  //   B
  //   B
  //   C'
  //   B'
  //   B
  //   NOT
  //   A'
  //   A'
  //   A'
  //   NAND
  //   NAND
  //   NAND
  //   AND
  //   AND
  //   OR
  //   OR
  //   --------------- Zadanie ---------------
  //   --------------- DNF Y ---------------
  //   --------------- DNF Z ---------------
  //   --------------- KNF Y ---------------
  //   --------------- KNF Z ---------------
  //   XNOR
  //   XOR
  //   AND
  //   AND
  //   OR
  //   OR
  //   Y DNF
  //   Z DNF
  //   Z DNF
  //   Y KNF
  //   Y KNF
  //   Y KNF
  //   Z KNF
  //   Z KNF
  //   Z KNF
  //   Z KNF
endmodule
